// Logisim project initial_labs.circ as structural Verilog: 1 circuit, main circuit main
module main (
  input  A,
  input  B,
  output W,
  output X,
  output Y,
  output Z
);

  wire not_1_out;

  not not_1 (not_1_out, B);
  or or_1 (W, A, B);
  or or_2 (X, A, not_1_out);
  xnor xnor_1 (Y, A, B);

  assign Z = B;

  // Notes on the sheet:
  //   David Ludwig
  //   CLA 01
  //   x3plus6
endmodule
