// Logisim project PLDs.circ as structural Verilog
module PC_BUS (
  input  t0,
  input  t2,
  output PC_BUS
);

  or or_1 (PC_BUS, t0, t2);
endmodule

module PC_LD (
  input  t4,
  input  clock,
  input  d5,
  input  d6,
  input  z,
  output PC_LD
);

  wire and_1_out, not_1_out, or_1_out;

  and and_1 (and_1_out, z, d6);
  or or_1 (or_1_out, d5, and_1_out);
  not not_1 (not_1_out, clock);
  and and_2 (PC_LD, t4, or_1_out, not_1_out);
endmodule

module PC_INC (
  input  t1,
  input  t3,
  input  t4,
  input  d1,
  input  d2,
  input  d6,
  input  z,
  output PC_INC
);

  wire and_1_out, and_2_out, not_1_out, or_1_out;

  or or_1 (or_1_out, d1, d2);
  not not_1 (not_1_out, z);
  and and_1 (and_1_out, t3, or_1_out);
  or or_2 (PC_INC, t1, and_1_out, and_2_out);
  and and_2 (and_2_out, not_1_out, d6, t4);
endmodule

module AR_LD (
  input  t0,
  input  t2,
  input  t4,
  input  clock,
  input  d1,
  input  d2,
  output AR_LD
);

  wire and_1_out, not_1_out, or_1_out, or_2_out;

  or or_1 (or_1_out, d1, d2);
  and and_1 (and_1_out, t4, or_1_out);
  not not_1 (not_1_out, clock);
  or or_2 (or_2_out, t0, t2, and_1_out);
  and and_2 (AR_LD, not_1_out, or_2_out);
endmodule

module DR_BUS (
  input  t2,
  input  t4,
  input  t6,
  input  d1,
  input  d2,
  input  d5,
  input  d6,
  input  z,
  output DR_BUS
);

  wire and_1_out, and_2_out, and_3_out, or_1_out, or_2_out, or_3_out;

  and and_1 (and_1_out, z, d6);
  or or_1 (or_1_out, t4, t6);
  and and_2 (and_2_out, or_1_out, or_2_out);
  or or_2 (or_2_out, d1, d2);
  and and_3 (and_3_out, t4, or_3_out);
  or or_3 (or_3_out, d5, and_1_out);
  or or_4 (DR_BUS, t2, and_2_out, and_3_out);
endmodule

module DR_LD (
  input  t1,
  input  t3,
  input  t5,
  input  clock,
  input  d1,
  input  d2,
  input  d5,
  input  d6,
  input  z,
  output DR_LD
);

  wire and_1_out, and_2_out, and_3_out, not_1_out, or_1_out, or_2_out, or_3_out, or_4_out;

  and and_1 (and_1_out, z, d6);
  or or_1 (or_1_out, d1, d2);
  or or_2 (or_2_out, t3, t5);
  or or_3 (or_3_out, d5, and_1_out);
  and and_2 (and_2_out, or_1_out, or_2_out);
  and and_3 (and_3_out, t3, or_3_out);
  not not_1 (not_1_out, clock);
  and and_4 (DR_LD, not_1_out, or_4_out);
  or or_4 (or_4_out, t1, and_2_out, and_3_out);
endmodule
